# Fritzing sketch j5-raspberry-memory-game (saved by Fritzing 0.9.3b)
breadboards: 1

parts:
  Raspberry_Pi_3_Model_B+ = Raspberry Pi 3 [part_number=RPI-3-V1.2]  # not connected
  Raspberry_PI_GDIO_External_Board = T Cobbler Plus
  BUTTON_ORANGE = Pushbutton [package="[SMD]"]
  LED_ORANGE = LED - 3mm [color="Orange (620nm)" package="3 mm [THT]"]
  R1 = Resistor [tolerance=±5% resistance=10k package=THT]
  LED_GREEN = LED - 3mm [color="Green (555nm)" package="3 mm [THT]"]
  R2 = Resistor [tolerance=±5% resistance=10k package=THT]
  LED_YELLOW = LED - 3mm [color="Yellow (595nm)" package="3 mm [THT]"]
  R3 = Resistor [tolerance=±5% resistance=10k package=THT]
  LED_BLUE = LED - 3mm [color="Blue (430nm)" package="3 mm [THT]"]
  R4 = Resistor [tolerance=±5% resistance=10k package=THT]
  R5 = Resistor [tolerance=±5% resistance=10k package=THT]
  BUTTON_YELLOW = Pushbutton [package="[SMD]"]
  R6 = Resistor [tolerance=±5% resistance=10k package=THT]
  BUTTON_GREEN = Pushbutton [package="[SMD]"]
  R7 = Resistor [tolerance=±5% resistance=10k package=THT]
  PIEZO = Piezo Speaker

nets:
  N1: Raspberry_PI_GDIO_External_Board.5.0V#3, BUTTON_ORANGE.Pin_3, BUTTON_ORANGE.Pin_4, BUTTON_YELLOW.Pin_3, BUTTON_YELLOW.Pin_4, BUTTON_GREEN.Pin_3, BUTTON_GREEN.Pin_4
  N2: Raspberry_PI_GDIO_External_Board.GND#5, LED_ORANGE.cathode, LED_YELLOW.cathode, LED_BLUE.cathode, R5.Pin_0, R6.Pin_0, R7.Pin_0, PIEZO.pin1
  N3: Raspberry_PI_GDIO_External_Board.#17, LED_ORANGE.anode, R1.Pin_0, R1.Pin_1
  N4: Raspberry_PI_GDIO_External_Board.#18, LED_BLUE.anode, R4.Pin_0, R4.Pin_1
  N5: Raspberry_PI_GDIO_External_Board.#27, LED_GREEN.anode, R2.Pin_0, R2.Pin_1
  N6: Raspberry_PI_GDIO_External_Board.#22, LED_YELLOW.anode, R3.Pin_0, R3.Pin_1
  N7: Raspberry_PI_GDIO_External_Board.#23, BUTTON_ORANGE.Pin_1, BUTTON_ORANGE.Pin_2, R5.Pin_1
  N8: Raspberry_PI_GDIO_External_Board.#24, BUTTON_GREEN.Pin_1, BUTTON_GREEN.Pin_2, R7.Pin_1
  N9: Raspberry_PI_GDIO_External_Board.#25, BUTTON_YELLOW.Pin_1, BUTTON_YELLOW.Pin_2, R6.Pin_1
  N10: Raspberry_PI_GDIO_External_Board.#16, PIEZO.pin2

custom parts:
  T Cobbler Plus: The T-Cobbler Plus is an add on prototyping board from Adafruit specifically designed for the Raspberry Pi B+ that can break out all those tasty power, GPIO, I2C and SPI pins from the 40-pin header onto a solderless breadboard. This set will make "cobbling together" prototypes with the Pi super easy. The T-Cobbler Plus can plug into any solderless breadboard.
